// Logisim project cpu.circ as structural Verilog: 4 circuits, main circuit main
module main (
  input  [31:0] INSTRUCTION,
  input  CLOCK,
  output [31:0] FETCH_ADDRESS,
  output [31:0] ra,
  output [31:0] sp,
  output [31:0] t0,
  output [31:0] t1,
  output [31:0] t2,
  output [31:0] s0,
  output [31:0] s1,
  output [31:0] a0
);

  wire branchcomp_1_breq, branchcomp_1_brlt, control_1_asel, control_1_brun, control_1_bsel, control_1_memrw,
       control_1_pcsel, control_1_regwen, register_2_q;
  wire [1:0] control_1_wbsel;
  wire [2:0] control_1_immsel, control_1_loadsel;
  wire [3:0] control_1_alusel;
  wire [31:0] adder_1_out, adder_2_out, Arithmetic_Logic_Unit_result, bit_extender_1_out, bit_extender_2_out,
       bit_extender_3_out, bit_extender_4_out, DMEM_readdata, immgen_1_imm, inst1, multiplexer_1_out,
       multiplexer_3_out, multiplexer_4_out, multiplexer_5_out, multiplexer_6_out, PC_q, RegFile_read_data_1,
       RegFile_read_data_2, register_1_q, register_3_q;

  Adder #(.width(32)) adder_1 (.a(PC_q), .b(32'h4), .out(adder_1_out));  // open: cin, cout
  Register #(.width(32)) PC (.D(multiplexer_1_out), .en(1'b1), .clk(CLOCK), .Q(PC_q));  // open: clr
  Multiplexer #(.width(32), .enable("false")) multiplexer_1 (
    .in0(adder_1_out), .in1(Arithmetic_Logic_Unit_result), .out(multiplexer_1_out), .sel(control_1_pcsel));
  Register #(.width(32)) register_1 (.D(INSTRUCTION), .en(1'b1), .clk(CLOCK), .Q(register_1_q));  // open: clr
  Register #(.width(1)) register_2 (.D(control_1_pcsel), .en(1'b1), .clk(CLOCK), .Q(register_2_q));  // open: clr
  Register #(.width(32)) register_3 (.D(PC_q), .en(1'b1), .clk(CLOCK), .Q(register_3_q));  // open: clr
  Divider #(.width(32)) divider_1 (.a(PC_q), .b(32'h4), .out(FETCH_ADDRESS));  // open: upper, rem
  Multiplexer #(.width(32), .enable("false")) multiplexer_2 (
    .in0(register_1_q), .in1(32'h13), .out(inst1), .sel(register_2_q));
  control control_1 (
    .inst(inst1), .BrLT(branchcomp_1_brlt), .BrEq(branchcomp_1_breq), .PCSel(control_1_pcsel),
    .ImmSel(control_1_immsel), .RegWEn(control_1_regwen), .BrUn(control_1_brun), .Asel(control_1_asel),
    .Bsel(control_1_bsel), .ALUsel(control_1_alusel), .MemRW(control_1_memrw), .loadsel(control_1_loadsel),
    .WBSel(control_1_wbsel));
  immGen immgen_1 (.ImmSel(control_1_immsel), .inst(inst1), .imm(immgen_1_imm));
  regfile_main RegFile (
    .Read_Register_1_rs1(inst1[19:15]), .Read_Register_2_rs2(inst1[24:20]), .Write_Register_rd(inst1[11:7]),
    .Write_Data(multiplexer_6_out), .Write_Enable(control_1_regwen), .Clock(CLOCK),
    .Read_Data_1(RegFile_read_data_1), .Read_Data_2(RegFile_read_data_2), .ra(ra), .sp(sp), .t0(t0), .t1(t1),
    .t2(t2), .s0(s0), .s1(s1), .a0(a0));
  Multiplexer #(.width(32), .enable("false")) multiplexer_3 (
    .in0(RegFile_read_data_1), .in1(register_3_q), .out(multiplexer_3_out), .sel(control_1_asel));
  Multiplexer #(.width(32), .enable("false")) multiplexer_4 (
    .in0(RegFile_read_data_2), .in1(immgen_1_imm), .out(multiplexer_4_out), .sel(control_1_bsel));
  BranchComp branchcomp_1 (
    .dataA(RegFile_read_data_1), .dataB(RegFile_read_data_2), .brun(control_1_brun),
    .BrEq(branchcomp_1_breq), .BrLT(branchcomp_1_brlt));
  alu Arithmetic_Logic_Unit (
    .A(multiplexer_3_out), .B(multiplexer_4_out), .ALUSel(control_1_alusel),
    .Result(Arithmetic_Logic_Unit_result));
  Adder #(.width(32)) adder_2 (.a(register_3_q), .b(32'h4), .out(adder_2_out));  // open: cin, cout
  mem_main DMEM (
    .WriteAddr(Arithmetic_Logic_Unit_result), .WriteData(RegFile_read_data_2), .MemRW(control_1_memrw),
    .ReadData(DMEM_readdata), .clk(CLOCK));
  assign bit_extender_1_out = {{24{DMEM_readdata[7]}}, DMEM_readdata[7:0]};  // Bit_Extender bit_extender_1
  assign bit_extender_2_out = {{16{DMEM_readdata[15]}}, DMEM_readdata[15:0]};  // Bit_Extender bit_extender_2
  assign bit_extender_3_out = {{24{1'b0}}, DMEM_readdata[7:0]};  // Bit_Extender bit_extender_3
  assign bit_extender_4_out = {{16{1'b0}}, DMEM_readdata[15:0]};  // Bit_Extender bit_extender_4
  Multiplexer #(.select(3), .width(32), .enable("false")) multiplexer_5 (
    .in0(bit_extender_1_out), .in1(bit_extender_2_out), .in2(DMEM_readdata), .in4(bit_extender_3_out),
    .in5(bit_extender_4_out), .out(multiplexer_5_out), .sel(control_1_loadsel));  // open: in3, in6, in7
  Multiplexer #(.select(2), .width(32), .enable("false")) multiplexer_6 (
    .in0(multiplexer_5_out), .in1(Arithmetic_Logic_Unit_result), .in2(adder_2_out), .out(multiplexer_6_out),
    .sel(control_1_wbsel));  // open: in3

  // Other names for the same wires on the sheet: clk = CLOCK; fetch_addr[31:0] = FETCH_ADDRESS

  // Notes on the sheet:
  //   Output
  //   Inputs/Outputs from run.circ. DO NOT MOVE THESE.
  //   Inputs
  //   Inputs/Outputs from run.circ. DO NOT MOVE THESE.
endmodule

module control (
  input  [31:0] inst,
  input  BrLT,
  input  BrEq,
  output PCSel,
  output [2:0] ImmSel,
  output RegWEn,
  output BrUn,
  output Asel,
  output Bsel,
  output [3:0] ALUsel,
  output MemRW,
  output [2:0] loadsel,
  output [1:0] WBSel
);

  wire and_1_out, and_2_out, and_3_out, and_4_out, and_5_out, and_6_out, and_7_out, and_8_out, and_9_out,
       and_10_out, and_11_out, and_12_out, and_13_out, and_14_out, and_15_out, and_16_out, and_17_out,
       and_18_out, and_19_out, and_20_out, and_21_out, and_22_out, and_23_out, and_24_out, and_25_out,
       and_26_out, and_27_out, and_28_out, comparator_1_eq, comparator_2_eq, comparator_3_eq,
       comparator_4_eq, comparator_5_eq, comparator_6_eq, comparator_7_eq, comparator_8_eq, comparator_9_eq,
       comparator_10_eq, comparator_11_eq, comparator_12_eq, comparator_13_eq, comparator_14_eq,
       comparator_15_eq, comparator_16_eq, comparator_17_eq, comparator_18_eq, comparator_19_eq,
       comparator_20_eq, comparator_21_eq, comparator_22_eq, comparator_23_eq, comparator_24_eq,
       comparator_25_eq, comparator_26_eq, comparator_27_eq, comparator_28_eq, comparator_29_eq,
       comparator_30_eq, comparator_31_eq, comparator_32_eq, comparator_33_eq, comparator_34_eq,
       comparator_35_eq, comparator_36_eq, comparator_37_eq, comparator_38_eq, comparator_39_eq,
       comparator_40_eq, comparator_41_eq, comparator_42_eq, comparator_43_eq, comparator_44_eq,
       comparator_45_eq, comparator_46_eq, comparator_47_eq, comparator_48_eq, comparator_49_eq,
       comparator_50_eq, comparator_51_eq, comparator_52_eq, comparator_53_eq, comparator_54_eq,
       comparator_55_eq, comparator_56_eq, comparator_57_eq, comparator_58_eq, comparator_59_eq,
       comparator_60_eq, comparator_61_eq, comparator_62_eq, comparator_63_eq, comparator_64_eq,
       comparator_65_eq, comparator_66_eq, comparator_67_eq, comparator_68_eq, comparator_69_eq,
       comparator_70_eq, comparator_71_eq, comparator_72_eq, comparator_73_eq, comparator_74_eq,
       comparator_75_eq, comparator_76_eq, comparator_77_eq, comparator_78_eq, comparator_79_eq,
       comparator_80_eq, comparator_81_eq, comparator_82_eq, comparator_83_eq, comparator_85_eq,
       comparator_86_eq, comparator_87_eq, comparator_88_eq, comparator_89_eq, comparator_90_eq,
       comparator_91_eq, comparator_92_eq, comparator_93_eq, comparator_94_eq, comparator_95_eq, not_1_out,
       not_2_out, or_1_out, or_2_out, or_4_out, or_5_out, or_6_out, or_7_out, or_8_out, or_9_out, or_10_out,
       or_11_out, or_12_out, or_13_out, or_16_out;
  wire [2:0] comparator_84_eq, multiplexer_1_out, multiplexer_2_out, multiplexer_3_out, multiplexer_4_out,
       multiplexer_5_out;
  wire [4:0] bit_extender_1_out, bit_extender_2_out, bit_extender_3_out, bit_extender_4_out,
       bit_extender_5_out, bit_extender_6_out, bit_extender_7_out, bit_extender_8_out, bit_extender_9_out,
       bit_extender_10_out, bit_extender_11_out, bit_extender_12_out, bit_extender_13_out,
       bit_extender_14_out, bit_extender_15_out, multiplier_1_out, multiplier_2_out, multiplier_3_out,
       multiplier_4_out, multiplier_5_out, multiplier_6_out, multiplier_7_out, multiplier_8_out,
       multiplier_9_out, multiplier_10_out, multiplier_11_out, multiplier_12_out, multiplier_13_out,
       multiplier_14_out, multiplier_15_out;
  wire [4:4] or_15_out;

  Comparator #(.width(7)) comparator_1 (.a(inst[6:0]), .b(7'b0000011), .eq(comparator_1_eq));  // open: gt, lt
  Comparator #(.width(7)) comparator_2 (.a(inst[6:0]), .b(7'b0010011), .eq(comparator_2_eq));  // open: gt, lt
  Comparator #(.width(7)) comparator_3 (.a(inst[6:0]), .b(7'b1100111), .eq(comparator_3_eq));  // open: gt, lt
  Comparator #(.width(7)) comparator_4 (.a(inst[6:0]), .b(7'b0100011), .eq(comparator_4_eq));  // open: gt, lt
  Comparator #(.width(7)) comparator_5 (.a(inst[6:0]), .b(7'b1100011), .eq(comparator_5_eq));  // open: gt, lt
  Comparator #(.width(7)) comparator_6 (.a(inst[6:0]), .b(7'b0010111), .eq(comparator_6_eq));  // open: gt, lt
  Comparator #(.width(7)) comparator_7 (.a(inst[6:0]), .b(7'b0110111), .eq(comparator_7_eq));  // open: gt, lt
  Comparator #(.width(7)) comparator_8 (.a(inst[6:0]), .b(7'b1101111), .eq(comparator_8_eq));  // open: gt, lt
  or or_1 (or_1_out, comparator_1_eq, comparator_2_eq, comparator_3_eq);
  or or_2 (or_2_out, comparator_6_eq, comparator_7_eq);
  Multiplexer #(.width(3), .enable("false")) multiplexer_1 (
    .in0(3'b000), .in1(3'b000), .out(multiplexer_1_out), .sel(or_1_out));
  Multiplexer #(.width(3), .enable("false")) multiplexer_2 (
    .in0(3'b000), .in1(3'b001), .out(multiplexer_2_out), .sel(comparator_4_eq));
  Multiplexer #(.width(3), .enable("false")) multiplexer_3 (
    .in0(3'b000), .in1(3'b010), .out(multiplexer_3_out), .sel(comparator_5_eq));
  Multiplexer #(.width(3), .enable("false")) multiplexer_4 (
    .in0(3'b000), .in1(3'b011), .out(multiplexer_4_out), .sel(or_2_out));
  Multiplexer #(.width(3), .enable("false")) multiplexer_5 (
    .in0(3'b000), .in1(3'b100), .out(multiplexer_5_out), .sel(comparator_8_eq));
  Comparator #(.width(7)) comparator_9 (.a(inst[6:0]), .b(7'b0110011), .eq(comparator_9_eq));  // open: gt, lt
  Comparator #(.width(3)) comparator_10 (.a(inst[14:12]), .b(3'b111), .eq(comparator_10_eq));  // open: gt, lt
  Comparator #(.width(7)) comparator_11 (.a(inst[31:25]), .b({7{1'b0}}), .eq(comparator_11_eq));  // open: gt, lt
  Comparator #(.width(7)) comparator_12 (.a(inst[6:0]), .b(7'b0010011), .eq(comparator_12_eq));  // open: gt, lt
  Comparator #(.width(3)) comparator_13 (.a(inst[14:12]), .b(3'b111), .eq(comparator_13_eq));  // open: gt, lt
  Comparator #(.width(7)) comparator_14 (.a(inst[6:0]), .b(7'b0110011), .eq(comparator_14_eq));  // open: gt, lt
  Comparator #(.width(3)) comparator_15 (.a(inst[14:12]), .b(3'b110), .eq(comparator_15_eq));  // open: gt, lt
  Comparator #(.width(7)) comparator_16 (.a(inst[31:25]), .b({7{1'b0}}), .eq(comparator_16_eq));  // open: gt, lt
  Comparator #(.width(7)) comparator_17 (.a(inst[6:0]), .b(7'b0010011), .eq(comparator_17_eq));  // open: gt, lt
  Comparator #(.width(3)) comparator_18 (.a(inst[14:12]), .b(3'b110), .eq(comparator_18_eq));  // open: gt, lt
  Comparator #(.width(7)) comparator_19 (.a(inst[6:0]), .b(7'b0110011), .eq(comparator_19_eq));  // open: gt, lt
  Comparator #(.width(3)) comparator_20 (.a(inst[14:12]), .b(3'b100), .eq(comparator_20_eq));  // open: gt, lt
  Comparator #(.width(7)) comparator_21 (.a(inst[31:25]), .b({7{1'b0}}), .eq(comparator_21_eq));  // open: gt, lt
  Comparator #(.width(7)) comparator_22 (.a(inst[6:0]), .b(7'b0010011), .eq(comparator_22_eq));  // open: gt, lt
  Comparator #(.width(3)) comparator_23 (.a(inst[14:12]), .b(3'b100), .eq(comparator_23_eq));  // open: gt, lt
  Comparator #(.width(7)) comparator_24 (.a(inst[6:0]), .b(7'b0110011), .eq(comparator_24_eq));  // open: gt, lt
  Comparator #(.width(3)) comparator_25 (.a(inst[14:12]), .b(3'b000), .eq(comparator_25_eq));  // open: gt, lt
  Comparator #(.width(7)) comparator_26 (.a(inst[31:25]), .b({7{1'b0}}), .eq(comparator_26_eq));  // open: gt, lt
  Comparator #(.width(7)) comparator_27 (.a(inst[6:0]), .b(7'b0010011), .eq(comparator_27_eq));  // open: gt, lt
  Comparator #(.width(3)) comparator_28 (.a(inst[14:12]), .b(3'b000), .eq(comparator_28_eq));  // open: gt, lt
  Comparator #(.width(7)) comparator_29 (.a(inst[6:0]), .b(7'b0100011), .eq(comparator_29_eq));  // open: gt, lt
  Comparator #(.width(3)) comparator_30 (.a(inst[14:12]), .b(3'b010), .eq(comparator_30_eq));  // open: gt, lt
  Comparator #(.width(7)) comparator_31 (.a(inst[6:0]), .b(7'b0000011), .eq(comparator_31_eq));  // open: gt, lt
  Comparator #(.width(7)) comparator_32 (.a(inst[6:0]), .b(7'b1100011), .eq(comparator_32_eq));  // open: gt, lt
  Comparator #(.width(7)) comparator_33 (.a(inst[6:0]), .b(7'b0010111), .eq(comparator_33_eq));  // open: gt, lt
  Comparator #(.width(7)) comparator_34 (.a(inst[6:0]), .b(7'b1101111), .eq(comparator_34_eq));  // open: gt, lt
  Comparator #(.width(7)) comparator_35 (.a(inst[6:0]), .b(7'b1100111), .eq(comparator_35_eq));  // open: gt, lt
  Comparator #(.width(7)) comparator_36 (.a(inst[6:0]), .b(7'b0110011), .eq(comparator_36_eq));  // open: gt, lt
  Comparator #(.width(3)) comparator_37 (.a(inst[14:12]), .b(3'b000), .eq(comparator_37_eq));  // open: gt, lt
  Comparator #(.width(7)) comparator_38 (.a(inst[31:25]), .b(7'b0100000), .eq(comparator_38_eq));  // open: gt, lt
  Comparator #(.width(7)) comparator_39 (.a(inst[6:0]), .b(7'b0110011), .eq(comparator_39_eq));  // open: gt, lt
  Comparator #(.width(3)) comparator_40 (.a(inst[14:12]), .b(3'b000), .eq(comparator_40_eq));  // open: gt, lt
  Comparator #(.width(7)) comparator_41 (.a(inst[31:25]), .b(7'b0000001), .eq(comparator_41_eq));  // open: gt, lt
  Comparator #(.width(7)) comparator_42 (.a(inst[6:0]), .b(7'b0110011), .eq(comparator_42_eq));  // open: gt, lt
  Comparator #(.width(3)) comparator_43 (.a(inst[14:12]), .b(3'b011), .eq(comparator_43_eq));  // open: gt, lt
  Comparator #(.width(7)) comparator_44 (.a(inst[31:25]), .b(7'b0000001), .eq(comparator_44_eq));  // open: gt, lt
  Comparator #(.width(7)) comparator_45 (.a(inst[6:0]), .b(7'b0110011), .eq(comparator_45_eq));  // open: gt, lt
  Comparator #(.width(3)) comparator_46 (.a(inst[14:12]), .b(3'b001), .eq(comparator_46_eq));  // open: gt, lt
  Comparator #(.width(7)) comparator_47 (.a(inst[31:25]), .b(7'b0000001), .eq(comparator_47_eq));  // open: gt, lt
  Comparator #(.width(7)) comparator_48 (.a(inst[6:0]), .b(7'b0110011), .eq(comparator_48_eq));  // open: gt, lt
  Comparator #(.width(3)) comparator_49 (.a(inst[14:12]), .b(3'b101), .eq(comparator_49_eq));  // open: gt, lt
  Comparator #(.width(7)) comparator_50 (.a(inst[31:25]), .b(7'b0000001), .eq(comparator_50_eq));  // open: gt, lt
  Comparator #(.width(7)) comparator_51 (.a(inst[6:0]), .b(7'b0110011), .eq(comparator_51_eq));  // open: gt, lt
  Comparator #(.width(3)) comparator_52 (.a(inst[14:12]), .b(3'b100), .eq(comparator_52_eq));  // open: gt, lt
  Comparator #(.width(7)) comparator_53 (.a(inst[31:25]), .b(7'b0000001), .eq(comparator_53_eq));  // open: gt, lt
  Comparator #(.width(7)) comparator_54 (.a(inst[6:0]), .b(7'b0110011), .eq(comparator_54_eq));  // open: gt, lt
  Comparator #(.width(3)) comparator_55 (.a(inst[14:12]), .b(3'b111), .eq(comparator_55_eq));  // open: gt, lt
  Comparator #(.width(7)) comparator_56 (.a(inst[31:25]), .b(7'b0000001), .eq(comparator_56_eq));  // open: gt, lt
  Comparator #(.width(7)) comparator_57 (.a(inst[6:0]), .b(7'b0110011), .eq(comparator_57_eq));  // open: gt, lt
  Comparator #(.width(3)) comparator_58 (.a(inst[14:12]), .b(3'b101), .eq(comparator_58_eq));  // open: gt, lt
  Comparator #(.width(7)) comparator_59 (.a(inst[31:25]), .b({7{1'b0}}), .eq(comparator_59_eq));  // open: gt, lt
  Comparator #(.width(7)) comparator_60 (.a(inst[6:0]), .b(7'b0010011), .eq(comparator_60_eq));  // open: gt, lt
  Comparator #(.width(3)) comparator_61 (.a(inst[14:12]), .b(3'b101), .eq(comparator_61_eq));  // open: gt, lt
  Comparator #(.width(7)) comparator_62 (.a(inst[6:0]), .b(7'b0010011), .eq(comparator_62_eq));  // open: gt, lt
  Comparator #(.width(3)) comparator_63 (.a(inst[14:12]), .b(3'b010), .eq(comparator_63_eq));  // open: gt, lt
  Comparator #(.width(7)) comparator_64 (.a(inst[6:0]), .b(7'b0110011), .eq(comparator_64_eq));  // open: gt, lt
  Comparator #(.width(3)) comparator_65 (.a(inst[14:12]), .b(3'b001), .eq(comparator_65_eq));  // open: gt, lt
  Comparator #(.width(7)) comparator_66 (.a(inst[31:25]), .b({7{1'b0}}), .eq(comparator_66_eq));  // open: gt, lt
  Comparator #(.width(7)) comparator_67 (.a(inst[6:0]), .b(7'b0010011), .eq(comparator_67_eq));  // open: gt, lt
  Comparator #(.width(3)) comparator_68 (.a(inst[14:12]), .b(3'b001), .eq(comparator_68_eq));  // open: gt, lt
  Comparator #(.width(7)) comparator_69 (.a(inst[31:25]), .b({7{1'b0}}), .eq(comparator_69_eq));  // open: gt, lt
  Comparator #(.width(7)) comparator_70 (.a(inst[6:0]), .b(7'b0110111), .eq(comparator_70_eq));  // open: gt, lt
  and and_1 (and_1_out, comparator_9_eq, comparator_10_eq, comparator_11_eq);
  and and_2 (and_2_out, comparator_12_eq, comparator_13_eq);
  and and_3 (and_3_out, comparator_14_eq, comparator_15_eq, comparator_16_eq);
  and and_4 (and_4_out, comparator_17_eq, comparator_18_eq);
  and and_5 (and_5_out, comparator_19_eq, comparator_20_eq, comparator_21_eq);
  and and_6 (and_6_out, comparator_22_eq, comparator_23_eq);
  and and_7 (and_7_out, comparator_24_eq, comparator_25_eq, comparator_26_eq);
  and and_8 (and_8_out, comparator_27_eq, comparator_28_eq);
  and and_9 (and_9_out, comparator_29_eq, comparator_30_eq);
  and and_10 (and_10_out, comparator_36_eq, comparator_37_eq, comparator_38_eq);
  and and_11 (and_11_out, comparator_39_eq, comparator_40_eq, comparator_41_eq);
  and and_12 (and_12_out, comparator_42_eq, comparator_43_eq, comparator_44_eq);
  and and_13 (and_13_out, comparator_45_eq, comparator_46_eq, comparator_47_eq);
  and and_14 (and_14_out, comparator_48_eq, comparator_49_eq, comparator_50_eq);
  and and_15 (and_15_out, comparator_51_eq, comparator_52_eq, comparator_53_eq);
  and and_16 (and_16_out, comparator_54_eq, comparator_55_eq, comparator_56_eq);
  and and_17 (and_17_out, comparator_57_eq, comparator_58_eq, comparator_59_eq);
  and and_18 (and_18_out, comparator_60_eq, comparator_61_eq);
  and and_19 (and_19_out, comparator_62_eq, comparator_63_eq);
  and and_20 (and_20_out, comparator_64_eq, comparator_65_eq, comparator_66_eq);
  and and_21 (and_21_out, comparator_67_eq, comparator_68_eq, comparator_69_eq);
  assign ImmSel = multiplexer_1_out | multiplexer_2_out | multiplexer_3_out | multiplexer_4_out | multiplexer_5_out;  // OR_Gate or_3, 3 bits wide
  or or_4 (or_4_out, and_1_out, and_2_out);
  or or_5 (or_5_out, and_3_out, and_4_out);
  or or_6 (or_6_out, and_5_out, and_6_out);
  assign bit_extender_1_out = {{4{1'b0}}, comparator_70_eq};  // Bit_Extender bit_extender_1
  or or_7 (or_7_out, and_7_out, and_8_out, and_9_out, comparator_31_eq, comparator_32_eq, comparator_33_eq, comparator_34_eq, comparator_35_eq);
  assign bit_extender_2_out = {{4{1'b0}}, and_10_out};  // Bit_Extender bit_extender_2
  assign bit_extender_3_out = {{4{1'b0}}, and_11_out};  // Bit_Extender bit_extender_3
  assign bit_extender_4_out = {{4{1'b0}}, and_12_out};  // Bit_Extender bit_extender_4
  assign bit_extender_5_out = {{4{1'b0}}, and_13_out};  // Bit_Extender bit_extender_5
  assign bit_extender_6_out = {{4{1'b0}}, and_14_out};  // Bit_Extender bit_extender_6
  assign bit_extender_7_out = {{4{1'b0}}, and_15_out};  // Bit_Extender bit_extender_7
  assign bit_extender_8_out = {{4{1'b0}}, and_16_out};  // Bit_Extender bit_extender_8
  or or_8 (or_8_out, and_20_out, and_21_out);
  Multiplier #(.width(5)) multiplier_1 (
    .a(bit_extender_1_out), .b(5'b01111), .out(multiplier_1_out));  // open: cin, cout
  assign bit_extender_9_out = {{4{1'b0}}, or_4_out};  // Bit_Extender bit_extender_9
  assign bit_extender_10_out = {{4{1'b0}}, or_5_out};  // Bit_Extender bit_extender_10
  assign bit_extender_11_out = {{4{1'b0}}, or_6_out};  // Bit_Extender bit_extender_11
  or or_9 (or_9_out, and_17_out, and_18_out);
  assign bit_extender_12_out = {{4{1'b0}}, and_19_out};  // Bit_Extender bit_extender_12
  Multiplier #(.width(5)) multiplier_2 (
    .a(bit_extender_9_out), .b({5{1'b0}}), .out(multiplier_2_out));  // open: cin, cout
  Multiplier #(.width(5)) multiplier_3 (
    .a(bit_extender_10_out), .b(5'b00001), .out(multiplier_3_out));  // open: cin, cout
  Multiplier #(.width(5)) multiplier_4 (
    .a(bit_extender_11_out), .b(5'b00010), .out(multiplier_4_out));  // open: cin, cout
  assign bit_extender_13_out = {{4{1'b0}}, or_7_out};  // Bit_Extender bit_extender_13
  Multiplier #(.width(5)) multiplier_5 (
    .a(bit_extender_2_out), .b(5'b00100), .out(multiplier_5_out));  // open: cin, cout
  Multiplier #(.width(5)) multiplier_6 (
    .a(bit_extender_3_out), .b(5'b00101), .out(multiplier_6_out));  // open: cin, cout
  Multiplier #(.width(5)) multiplier_7 (
    .a(bit_extender_4_out), .b(5'b00110), .out(multiplier_7_out));  // open: cin, cout
  Multiplier #(.width(5)) multiplier_8 (
    .a(bit_extender_5_out), .b(5'b00111), .out(multiplier_8_out));  // open: cin, cout
  Multiplier #(.width(5)) multiplier_9 (
    .a(bit_extender_6_out), .b(5'b01000), .out(multiplier_9_out));  // open: cin, cout
  Multiplier #(.width(5)) multiplier_10 (
    .a(bit_extender_7_out), .b(5'b01001), .out(multiplier_10_out));  // open: cin, cout
  Multiplier #(.width(5)) multiplier_11 (
    .a(bit_extender_8_out), .b(5'b01010), .out(multiplier_11_out));  // open: cin, cout
  Multiplier #(.width(5)) multiplier_12 (
    .a(bit_extender_12_out), .b(5'b01101), .out(multiplier_12_out));  // open: cin, cout
  assign bit_extender_14_out = {{4{1'b0}}, or_8_out};  // Bit_Extender bit_extender_14
  Comparator #(.width(7)) comparator_71 (.a(inst[6:0]), .b(7'b0100011), .eq(comparator_71_eq));  // open: gt, lt
  Comparator #(.width(7)) comparator_72 (.a(inst[6:0]), .b(7'b1100011), .eq(comparator_72_eq));  // open: gt, lt
  Comparator #(.width(7)) comparator_73 (.a(inst[6:0]), .b(7'b1101111), .eq(comparator_73_eq));  // open: gt, lt
  Comparator #(.width(7)) comparator_74 (.a(inst[6:0]), .b(7'b1100111), .eq(comparator_74_eq));  // open: gt, lt
  Comparator #(.width(7)) comparator_75 (.a(inst[6:0]), .b(7'b1100011), .eq(comparator_75_eq));  // open: gt, lt
  Comparator #(.width(3)) comparator_76 (.a(inst[14:12]), .b(3'b000), .eq(comparator_76_eq));  // open: gt, lt
  Comparator #(.width(3)) comparator_77 (.a(inst[14:12]), .b(3'b001), .eq(comparator_77_eq));  // open: gt, lt
  Comparator #(.width(3)) comparator_78 (.a(inst[14:12]), .b(3'b100), .eq(comparator_78_eq));  // open: gt, lt
  Comparator #(.width(3)) comparator_79 (.a(inst[14:12]), .b(3'b110), .eq(comparator_79_eq));  // open: gt, lt
  Comparator #(.width(3)) comparator_80 (.a(inst[14:12]), .b(3'b111), .eq(comparator_80_eq));  // open: gt, lt
  assign bit_extender_15_out = {{4{1'b0}}, or_9_out};  // Bit_Extender bit_extender_15
  Multiplier #(.width(5)) multiplier_13 (
    .a(bit_extender_14_out), .b(5'b01110), .out(multiplier_13_out));  // open: cin, cout
  Comparator #(.width(7)) comparator_81 (.a(inst[6:0]), .b(7'b1100011), .eq(comparator_81_eq));  // open: gt, lt
  Comparator #(.width(3)) comparator_82 (.a(inst[14:12]), .b(3'b110), .eq(comparator_82_eq));  // open: gt, lt
  Comparator #(.width(3)) comparator_83 (.a(inst[14:12]), .b(3'b111), .eq(comparator_83_eq));  // open: gt, lt
  or or_10 (or_10_out, comparator_73_eq, comparator_74_eq);
  not not_1 (not_1_out, BrEq);
  not not_2 (not_2_out, BrLT);
  Multiplier #(.width(5)) multiplier_14 (
    .a(bit_extender_13_out), .b(5'b00011), .out(multiplier_14_out));  // open: cin, cout
  Multiplier #(.width(5)) multiplier_15 (
    .a(bit_extender_15_out), .b(5'b01011), .out(multiplier_15_out));  // open: cin, cout
  or or_11 (or_11_out, comparator_71_eq, comparator_72_eq);
  or or_12 (or_12_out, comparator_82_eq, comparator_83_eq);
  and and_22 (and_22_out, BrEq, comparator_76_eq);
  and and_23 (and_23_out, not_1_out, comparator_77_eq);
  and and_24 (and_24_out, comparator_78_eq, BrLT);
  and and_25 (and_25_out, comparator_79_eq, BrLT);
  and and_26 (and_26_out, comparator_80_eq, not_2_out);
  Multiplexer #(.enable("false")) multiplexer_6 (.in0(1'b1), .in1(1'b0), .out(RegWEn), .sel(or_11_out));
  and and_27 (and_27_out, comparator_81_eq, or_12_out);
  or or_13 (or_13_out, and_22_out, and_23_out, and_24_out, and_25_out, and_26_out);
  Multiplexer #(.enable("false")) multiplexer_7 (.in0(1'b0), .in1(1'b1), .out(BrUn), .sel(and_27_out));
  and and_28 (and_28_out, comparator_75_eq, or_13_out);
  or or_14 (PCSel, or_10_out, and_28_out);
  Comparator #(.width(7)) comparator_84 (.a(inst[6:0]), .b(7'b0000011), .eq(comparator_84_eq[0]));  // open: gt, lt
  Comparator #(.width(7)) comparator_85 (.a(inst[6:0]), .b(7'b0010011), .eq(comparator_85_eq));  // open: gt, lt
  Comparator #(.width(7)) comparator_86 (.a(inst[6:0]), .b(7'b0010111), .eq(comparator_86_eq));  // open: gt, lt
  Comparator #(.width(7)) comparator_87 (.a(inst[6:0]), .b(7'b0110011), .eq(comparator_87_eq));  // open: gt, lt
  Comparator #(.width(7)) comparator_88 (.a(inst[6:0]), .b(7'b0110111), .eq(comparator_88_eq));  // open: gt, lt
  Comparator #(.width(7)) comparator_89 (.a(inst[6:0]), .b(7'b1101111), .eq(comparator_89_eq));  // open: gt, lt
  Comparator #(.width(7)) comparator_90 (.a(inst[6:0]), .b(7'b1100111), .eq(comparator_90_eq));  // open: gt, lt
  assign {or_15_out[4], ALUsel} = multiplier_2_out | multiplier_3_out | multiplier_4_out | multiplier_14_out | multiplier_5_out | multiplier_6_out | multiplier_7_out | multiplier_8_out | multiplier_9_out | multiplier_10_out | multiplier_11_out | multiplier_15_out | multiplier_12_out | multiplier_13_out | multiplier_1_out;  // OR_Gate or_15, 5 bits wide
  Comparator #(.width(7)) comparator_91 (.a(inst[6:0]), .b(7'b1100011), .eq(comparator_91_eq));  // open: gt, lt
  Comparator #(.width(7)) comparator_92 (.a(inst[6:0]), .b(7'b0010111), .eq(comparator_92_eq));  // open: gt, lt
  Comparator #(.width(7)) comparator_93 (.a(inst[6:0]), .b(7'b1101111), .eq(comparator_93_eq));  // open: gt, lt
  Comparator #(.width(7)) comparator_94 (.a(inst[6:0]), .b(7'b0110011), .eq(comparator_94_eq));  // open: gt, lt
  Comparator #(.width(7)) comparator_95 (.a(inst[6:0]), .b(7'b0100011), .eq(comparator_95_eq));  // open: gt, lt
  or or_16 (or_16_out, comparator_91_eq, comparator_92_eq, comparator_93_eq);
  Multiplexer #(.enable("false")) multiplexer_8 (.in0(1'b1), .in1(1'b0), .out(Bsel), .sel(comparator_94_eq));
  Multiplexer #(.enable("false")) multiplexer_9 (.in0(1'b0), .in1(1'b1), .out(MemRW), .sel(comparator_95_eq));
  or or_17 (comparator_84_eq[1], comparator_85_eq, comparator_86_eq, comparator_87_eq, comparator_88_eq);
  or or_18 (comparator_84_eq[2], comparator_89_eq, comparator_90_eq);
  Multiplexer #(.enable("false")) multiplexer_10 (.in0(1'b0), .in1(1'b1), .out(Asel), .sel(or_16_out));
  Multiplexer #(.select(3), .width(2), .enable("false")) multiplexer_11 (
    .in1(2'b00), .in2(2'b01), .in4(2'b10), .out(WBSel), .sel(comparator_84_eq));  // open: in0, in3, in5, in6, in7

  assign loadsel = inst[14:12];

  // Other names for the same wires on the sheet: opcode[6:0] = inst[6:0]; funct3[2:0] = inst[14:12];
  //   funct7[6:0] = inst[31:25]
endmodule

module immGen (
  input  [2:0] ImmSel,
  input  [31:0] inst,
  output [31:0] imm
);

  wire [31:0] bit_extender_1_out, bit_extender_2_out, bit_extender_3_out, bit_extender_4_out,
       bit_extender_5_out, shifter_1_out, shifter_2_out, shifter_3_out;

  assign bit_extender_1_out = {{20{inst[31]}}, {inst[31], inst[7], inst[30:25], inst[11:8]}};  // Bit_Extender bit_extender_1
  assign bit_extender_2_out = {{12{1'b0}}, inst[31:12]};  // Bit_Extender bit_extender_2
  assign bit_extender_3_out = {{20{inst[31]}}, inst[31:20]};  // Bit_Extender bit_extender_3
  Shifter #(.width(32)) shifter_1 (.in(bit_extender_2_out), .\dist (5'b01100), .out(shifter_1_out));
  assign bit_extender_4_out = {{12{inst[31]}}, {inst[31], inst[19:12], inst[20], inst[30:21]}};  // Bit_Extender bit_extender_4
  assign bit_extender_5_out = {{20{inst[31]}}, {inst[31:25], inst[11:7]}};  // Bit_Extender bit_extender_5
  Shifter #(.width(32)) shifter_2 (.in(bit_extender_1_out), .\dist (5'b00001), .out(shifter_2_out));
  Shifter #(.width(32)) shifter_3 (.in(bit_extender_4_out), .\dist (5'b00001), .out(shifter_3_out));
  Multiplexer #(.select(3), .width(32), .enable("false")) multiplexer_1 (
    .in0(bit_extender_3_out), .in1(bit_extender_5_out), .in2(shifter_2_out), .in3(shifter_1_out),
    .in4(shifter_3_out), .out(imm), .sel(ImmSel));  // open: in5, in6, in7
endmodule

module BranchComp (
  input  [31:0] dataA,
  input  [31:0] dataB,
  input  brun,
  output BrEq,
  output BrLT
);

  wire comparator_1_eq, comparator_2_eq, comparator_3_lt, comparator_4_lt;

  Comparator #(.width(32)) comparator_1 (.a(dataA), .b(dataB), .eq(comparator_1_eq));  // open: gt, lt
  Comparator #(.width(32), .mode("unsigned")) comparator_2 (
    .a(dataA), .b(dataB), .eq(comparator_2_eq));  // open: gt, lt
  Multiplexer #(.enable("false")) multiplexer_1 (.in0(comparator_1_eq), .in1(comparator_2_eq), .out(BrEq), .sel(brun));
  Comparator #(.width(32)) comparator_3 (.a(dataA), .b(dataB), .lt(comparator_3_lt));  // open: gt, eq
  Comparator #(.width(32), .mode("unsigned")) comparator_4 (
    .a(dataA), .b(dataB), .lt(comparator_4_lt));  // open: gt, eq
  Multiplexer #(.enable("false")) multiplexer_2 (.in0(comparator_3_lt), .in1(comparator_4_lt), .out(BrLT), .sel(brun));

  // Other names for the same wires on the sheet: bru = brun; da[31:0] = dataA; db[31:0] = dataB
endmodule
