// Logisim project alu.circ as structural Verilog: 9 circuits, main circuit alu
module alu (
  input  [31:0] A,
  input  [31:0] B,
  input  [3:0] ALUSel,
  output [31:0] Result
);

  wire not_1_out, sirr, sltt;
  wire [31:0] addd, andd, bit_extender_1_out, bit_extender_2_out, cntoo, divuu, divv, invert_1_out_2, mulhh,
       mulhuu, multt, num32_1_out_2, num32_2_out_2, orr, remuu, slll, sraa, srll, subb, xorr;

  assign andd = A & B;  // AND_Gate and_1, 32 bits wide
  assign orr = A | B;  // OR_Gate or_1, 32 bits wide
  assign xorr = A ^ B;  // XOR_Gate xor_1, 32 bits wide
  Adder #(.width(32)) adder_1 (.a(A), .b(B), .out(addd));  // open: cin, cout
  Subtractor #(.width(32)) subtractor_1 (.a(A), .b(B), .out(subb));  // open: bin, bout
  Shifter #(.width(32)) shifter_1 (.in(A), .\dist (B[4:0]), .out(slll));
  invert invert_1 (.in_1(B), .out_2(invert_1_out_2));
  Shifter #(.width(32), .shift("lr")) shifter_2 (.in(A), .\dist (B[4:0]), .out(srll));
  Shifter #(.width(32), .shift("ar")) shifter_3 (.in(A), .\dist (B[4:0]), .out(sraa));
  Comparator #(.width(32)) comparator_1 (.a(A), .b(B), .lt(sltt));  // open: gt, eq
  Comparator #(.width(32), .mode("unsigned")) comparator_2 (.a(A), .b(invert_1_out_2), .eq(sirr));  // open: gt, lt
  num32 num32_1 (.in_1(A), .out_2(num32_1_out_2));
  Adder #(.width(32)) adder_2 (.a(num32_1_out_2), .b(num32_2_out_2), .out(cntoo));  // open: cin, cout
  num32 num32_2 (.in_1(B), .out_2(num32_2_out_2));
  assign bit_extender_1_out = {{31{1'b0}}, sltt};  // Bit_Extender bit_extender_1
  Multiplier #(.width(32)) multiplier_1 (.a(A), .b(B), .cout(mulhuu));  // open: out, cin
  not not_1 (not_1_out, 1'b0);
  assign bit_extender_2_out = {{31{1'b0}}, not_1_out};  // Bit_Extender bit_extender_2
  Multiplexer #(.select(4), .width(32), .enable("false")) multiplexer_1 (
    .in0(andd), .in1(orr), .in2(xorr), .in3(addd), .in4(subb), .in5(multt), .in6(mulhuu), .in7(mulhh),
    .in8(divuu), .in9(divv), .in10(remuu), .in11(srll), .in12(sraa), .in13(bit_extender_1_out), .in14(slll),
    .in15(B), .out(Result), .sel(ALUSel));
  div div_1 (.a(A), .b(B), .out_5(divv));  // open: in_3, in_4
  sign sign_1 (.constand(bit_extender_2_out), .a(A), .b(B), .low(multt), .high(mulhh));  // open: in_4, in_5
  Divider #(.width(32)) divider_1 (.a(A), .b(B), .out(divuu), .rem(remuu));  // open: upper

  // Other names for the same wires on the sheet: lui[31:0] = B

  // Notes on the sheet:
  //   INPUTS to your circuit
  //   DON'T CHANGE THE LOCATIONS OF THE INPUTS AND OUTPUTS!
  //   OUTPUT from your circuit
endmodule

module invert (
  input  [31:0] in_1,
  output [31:0] out_2
);


  assign out_2 = {in_1[0], in_1[1], in_1[2], in_1[3], in_1[4], in_1[5], in_1[6], in_1[7], in_1[8], in_1[9], in_1[10], in_1[11], in_1[12], in_1[13], in_1[14], in_1[15], in_1[16], in_1[17], in_1[18], in_1[19], in_1[20], in_1[21], in_1[22], in_1[23], in_1[24], in_1[25], in_1[26], in_1[27], in_1[28], in_1[29], in_1[30], in_1[31]};
endmodule

module num32 (
  input  [31:0] in_1,
  output [31:0] out_2
);

  wire [31:0] num16_1_out_2, num16_2_out_2;

  num16 num16_1 (.in_1(in_1[15:0]), .out_2(num16_1_out_2));
  num16 num16_2 (.in_1(in_1[31:16]), .out_2(num16_2_out_2));
  Adder #(.width(32)) adder_1 (.a(num16_1_out_2), .b(num16_2_out_2), .out(out_2));  // open: cin, cout
endmodule

module num16 (
  input  [15:0] in_1,
  output [31:0] out_2
);

  wire [31:0] num8_1_out_2, num8_2_out_2;

  num8 num8_1 (.in_1(in_1[7:0]), .out_2(num8_1_out_2));
  num8 num8_2 (.in_1(in_1[15:8]), .out_2(num8_2_out_2));
  Adder #(.width(32)) adder_1 (.a(num8_1_out_2), .b(num8_2_out_2), .out(out_2));  // open: cin, cout
endmodule

module num8 (
  input  [7:0] in_1,
  output [31:0] out_2
);

  wire [31:0] num4_1_out_2, num4_2_out_2;

  num4 num4_1 (.in_1(in_1[3:0]), .out_2(num4_1_out_2));
  num4 num4_2 (.in_1(in_1[7:4]), .out_2(num4_2_out_2));
  Adder #(.width(32)) adder_1 (.a(num4_1_out_2), .b(num4_2_out_2), .out(out_2));  // open: cin, cout
endmodule

module num4 (
  input  [3:0] in_1,
  output [31:0] out_2
);

  wire [31:0] num2_1_out_2, num2_2_out_2;

  num2 num2_1 (.in_1(in_1[1:0]), .out_2(num2_1_out_2));
  num2 num2_2 (.in_1(in_1[3:2]), .out_2(num2_2_out_2));
  Adder #(.width(32)) adder_1 (.a(num2_1_out_2), .b(num2_2_out_2), .out(out_2));  // open: cin, cout
endmodule

module num2 (
  input  [1:0] in_1,
  output [31:0] out_2
);

  wire [1:0] adder_1_out;

  Adder #(.width(1)) adder_1 (.a(in_1[0]), .b(in_1[1]), .out(adder_1_out[0]), .cout(adder_1_out[1]));  // open: cin
  assign out_2 = {{30{1'b0}}, adder_1_out};  // Bit_Extender bit_extender_1
endmodule

module sign (
  input  [31:0] constand,
  input  [31:0] a,
  input  [31:0] b,
  input  in_4,
  input  in_5,
  output [31:0] low,
  output [31:0] high
);

  wire adder_1_cout, adder_2_cout, comparator_1_eq, comparator_2_eq;
  wire [1:0] not_2_out;
  wire [31:0] adder_1_out, adder_2_out, adder_3_out, adder_4_out, bit_extender_1_out, bit_extender_2_out,
       multiplier_1_cout, multiplier_1_out, multiplier_2_cout, multiplier_2_out, multiplier_3_cout,
       multiplier_3_out, multiplier_4_cout, multiplier_4_out, negator_1_out, negator_2_out, negator_3_out,
       negator_4_out, negator_5_out, negator_6_out, negator_7_out, negator_8_out, subtractor_1_out,
       subtractor_2_out, subtractor_3_out, subtractor_4_out;

  Comparator #(.width(1)) comparator_1 (.a(a[31]), .b(in_4), .eq(comparator_1_eq));  // open: gt, lt
  Comparator #(.width(1)) comparator_2 (.a(b[31]), .b(in_5), .eq(comparator_2_eq));  // open: gt, lt
  Negator #(.width(32)) negator_1 (.in(a), .out(negator_1_out));
  not not_1 (not_2_out[1], comparator_1_eq);
  not not_2 (not_2_out[0], comparator_2_eq);
  Negator #(.width(32)) negator_2 (.in(b), .out(negator_2_out));
  Multiplier #(.width(32)) multiplier_1 (
    .a(negator_1_out), .b(b), .out(multiplier_1_out), .cout(multiplier_1_cout));  // open: cin
  Multiplier #(.width(32)) multiplier_2 (.a(a), .b(b), .out(multiplier_2_out), .cout(multiplier_2_cout));  // open: cin
  Multiplier #(.width(32)) multiplier_3 (
    .a(a), .b(negator_2_out), .out(multiplier_3_out), .cout(multiplier_3_cout));  // open: cin
  Negator #(.width(32)) negator_3 (.in(multiplier_1_out), .out(negator_3_out));
  Negator #(.width(32)) negator_4 (.in(multiplier_1_cout), .out(negator_4_out));
  Negator #(.width(32)) negator_5 (.in(a), .out(negator_5_out));
  Negator #(.width(32)) negator_6 (.in(b), .out(negator_6_out));
  Negator #(.width(32)) negator_7 (.in(multiplier_3_out), .out(negator_7_out));
  Subtractor #(.width(32)) subtractor_1 (.a(negator_7_out), .b(constand), .out(subtractor_1_out));  // open: bin, bout
  Negator #(.width(32)) negator_8 (.in(multiplier_3_cout), .out(negator_8_out));
  Subtractor #(.width(32)) subtractor_2 (.a(negator_8_out), .b(constand), .out(subtractor_2_out));  // open: bin, bout
  Subtractor #(.width(32)) subtractor_3 (.a(negator_3_out), .b(constand), .out(subtractor_3_out));  // open: bin, bout
  Subtractor #(.width(32)) subtractor_4 (.a(negator_4_out), .b(constand), .out(subtractor_4_out));  // open: bin, bout
  assign bit_extender_1_out = {{31{1'b0}}, adder_2_cout};  // Bit_Extender bit_extender_1
  Adder #(.width(32)) adder_1 (
    .a(subtractor_3_out), .b(constand), .out(adder_1_out), .cout(adder_1_cout));  // open: cin
  assign bit_extender_2_out = {{31{1'b0}}, adder_1_cout};  // Bit_Extender bit_extender_2
  Multiplier #(.width(32)) multiplier_4 (
    .a(negator_5_out), .b(negator_6_out), .out(multiplier_4_out), .cout(multiplier_4_cout));  // open: cin
  Adder #(.width(32)) adder_2 (
    .a(subtractor_1_out), .b(constand), .out(adder_2_out), .cout(adder_2_cout));  // open: cin
  Adder #(.width(32)) adder_3 (.a(subtractor_2_out), .b(bit_extender_1_out), .out(adder_3_out));  // open: cin, cout
  Adder #(.width(32)) adder_4 (.a(subtractor_4_out), .b(bit_extender_2_out), .out(adder_4_out));  // open: cin, cout
  Multiplexer #(.select(2), .width(32), .enable("false")) multiplexer_1 (
    .in0(multiplier_2_out), .in1(adder_2_out), .in2(adder_1_out), .in3(multiplier_4_out), .out(low),
    .sel(not_2_out));
  Multiplexer #(.select(2), .width(32), .enable("false")) multiplexer_2 (
    .in0(multiplier_2_cout), .in1(adder_3_out), .in2(adder_4_out), .in3(multiplier_4_cout), .out(high),
    .sel(not_2_out));
endmodule

module div (
  input  [31:0] a,
  input  [31:0] b,
  input  in_3,
  input  in_4,
  output [31:0] out_5
);

  wire comparator_1_eq, comparator_2_eq;
  wire [1:0] not_2_out;
  wire [31:0] divider_1_out, divider_2_out, divider_3_out, divider_4_out, negator_1_out, negator_2_out,
       negator_3_out, negator_4_out, negator_5_out, negator_6_out;

  Comparator #(.width(1)) comparator_1 (.a(a[31]), .b(in_3), .eq(comparator_1_eq));  // open: gt, lt
  Comparator #(.width(1)) comparator_2 (.a(b[31]), .b(in_4), .eq(comparator_2_eq));  // open: gt, lt
  not not_1 (not_2_out[1], comparator_1_eq);
  not not_2 (not_2_out[0], comparator_2_eq);
  Divider #(.width(32)) divider_1 (.a(a), .b(b), .out(divider_1_out));  // open: upper, rem
  Negator #(.width(32)) negator_1 (.in(b), .out(negator_1_out));
  Negator #(.width(32)) negator_2 (.in(a), .out(negator_2_out));
  Divider #(.width(32)) divider_2 (.a(negator_2_out), .b(b), .out(divider_2_out));  // open: upper, rem
  Negator #(.width(32)) negator_3 (.in(a), .out(negator_3_out));
  Negator #(.width(32)) negator_4 (.in(b), .out(negator_4_out));
  Divider #(.width(32)) divider_3 (.a(a), .b(negator_1_out), .out(divider_3_out));  // open: upper, rem
  Divider #(.width(32)) divider_4 (.a(negator_3_out), .b(negator_4_out), .out(divider_4_out));  // open: upper, rem
  Negator #(.width(32)) negator_5 (.in(divider_3_out), .out(negator_5_out));
  Negator #(.width(32)) negator_6 (.in(divider_2_out), .out(negator_6_out));
  Multiplexer #(.select(2), .width(32), .enable("false")) multiplexer_1 (
    .in0(divider_1_out), .in1(negator_5_out), .in2(negator_6_out), .in3(divider_4_out), .out(out_5),
    .sel(not_2_out));
endmodule
